# Fritzing sketch activador (saved by Fritzing 0.9.3b)
breadboards: 1

parts:
  Part1 = Arduino Uno (Rev3)
  LCD1 = LCD screen
  R1 = Rotary Potentiometer (Small) [maximum_resistance=100kΩ package=THT]
  S1 = Toggle Switch [package=THT]
  S2 = Pushbutton [package=THT]
  R2 = Resistor [tolerance=±5% resistance=220 package=THT]
  R3 = Resistor [tolerance=±5% resistance=220 package=THT]
  R4 = Resistor [tolerance=±5% resistance=10k package=THT]
  R5 = Resistor [tolerance=±5% resistance=10k package=THT]
  C1 = Electrolytic Capacitor [capacitance=1µF package="100 mil [THT, electrolytic]"]
  J2 = Piezo Speaker

nets:
  N1: Part1.D8, J2.pin2
  GND: Part1.GND, LCD1.VSS, LCD1.LED-, R1.leg2, R2.Pin_1, R4.Pin_0, R5.Pin_0, C1.-
  N2: Part1.D2, LCD1.DB7
  N3: Part1.D3_PWM, LCD1.DB6
  N4: Part1.D4, LCD1.DB5
  N5: Part1.D5_PWM, LCD1.DB4
  N6: Part1.D6_PWM, S1.COM, R4.Pin_1
  N7: Part1.D7, S2.leg0, R5.Pin_1
  5V: Part1.5V, LCD1.VDD, R1.leg1, S1.L1, S2.leg1, R3.Pin_0, C1.+
  N8: LCD1.V0, R1.wiper
  N9: LCD1.LED+, R3.Pin_1
  N10: R2.Pin_0, J2.pin1
